# Fritzing sketch FlowerPot Fritz (saved by Fritzing 0.9.9b)
breadboards: 1

parts:
  Argon1 = Particle Argon
  OLED_I2C1 = OLED 128x64 I2C Monochrome Display
  WATER_PUMP1 = water pump/motor  # not connected
  SENS1 = SoilWatch 10  # not connected
  Grove1 = Grove Dust Sensor  # not connected
  Part1 = MQ-131 breakout  # not connected
  Part2 = Adafruit MicroSD card breakout board [part_number="Adafruit #254"]  # not connected
  Relay1 = Relay - 6 pins [package="DIP (Dual Inline) [THT]"]  # not connected

nets:
  3.3V: Argon1.3.3V, OLED_I2C1.VDD
  GND: Argon1.GND, OLED_I2C1.GND
  N1: Argon1.SDA, OLED_I2C1.SDA
  N2: Argon1.SCL, OLED_I2C1.SCK

custom parts:
  Particle Argon: The Argon is a powerful Wi-Fi enabled development board that can act as either a standalone Wi-Fi endpoint or Wi-Fi enabled gateway for Particle Mesh networks. It is based on the Nordic nRF52840 and has built-in battery charging circuitry so it’s easy to connect a Li-Po and deploy your local network in minutes. The Argon is great for connecting existing projects to the Particle Device Cloud or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
  water pump/motor: WATER PUMP BY ARDUBLOCKTR
  SoilWatch 10: SoilWatch 10 - Capacitive soil moisture sensor
  Grove Dust Sensor: PPD42 Grove Dust Sensor
  MQ-131 breakout: SKU: 101282
  Adafruit MicroSD card breakout board: Not just a simple breakout board, this microSD adapter goes the extra mile - designed for ease of use. Onboard 5v->3v regulator provides 150mA for power-hungry cards 3v level shifting means you can use this with ease on either 3v or 5v systems Uses a proper level shifting chip, not resistors: less problems, and faster read/write access Use 3 or 4 digital pins to read and write 2Gb+ of storage!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
  Relay - 6 pins: A DIP stand-in part for whatever IC you want. With 6 pins on a 900mil dual inline package (DIP) footprint.
